# Fritzing sketch CircuitoHeltecSensor (saved by Fritzing 0.9.3b)

parts:
  Heltec_Wireless_Stick1 = Heltec Wireless Stick [part_number=HTIT-WS]
  e-radionica1 = TCS230 Color Sensor [part_number=101209]

nets:
  N1: Heltec_Wireless_Stick1.pin5, e-radionica1.S0
  N2: Heltec_Wireless_Stick1.pin6, e-radionica1.S1
  N3: Heltec_Wireless_Stick1.pin_16, e-radionica1.Gnd
  N4: Heltec_Wireless_Stick1.pin_18, e-radionica1.Vcc
  N5: Heltec_Wireless_Stick1.pin_25, e-radionica1.S3
  N6: Heltec_Wireless_Stick1.pin_30, e-radionica1.S2
  N7: Heltec_Wireless_Stick1.pin_34, e-radionica1.Out

notes:
  Heltec Sensor
  GND = GND
  5 V = VCC
  GPIO39 = OUT
  GPIO12 = S0
  GPIO13 = S1
  GPIO17 = S2
  GPIO23 = S3

custom parts:
  Heltec Wireless Stick: Wireless Stick is a part of the Heltec LoRa series and incorporates an ESP32 processor, WiFi, SX1276 LoRa and Bluetooth with an integrated CP2102 USB to serial port interface and onboard SHT1.25 battery interface with integrated lithium battery management system.
  TCS230 Color Sensor: TCS230
